# Fritzing sketch ft232h (saved by Fritzing 0.9.6b)

parts:
  Part1 = Adafruit FT232H Breakout - USB C and STEMMA QT [part_number="Adafruit #2264"]
  Part2 = Adafruit SCD4x [part_number="Adafruit #5187"]

nets:
  GND: Part1.GND, Part2.GND
  +3V3: Part1.+3V3, Part2.VCC
  N1: Part1.D0/SCL/SCK, Part2.SCL
  N2: Part1.D1/SDA/MOSI, Part1.D2/SDA/MISO, Part2.SDA

custom parts:
  Adafruit FT232H Breakout - USB C and STEMMA QT: Wouldn't it be cool to drive a tiny OLED display, read a color sensor, or even just flash some LEDs directly from your computer? Sure you can program an Arduino or Trinket to talk to these devices and your computer, but why can't your computer just talk to those devices and sensors itself? Well, now your computer can talk to devices using the Adafruit FT232H breakout board! What can the FT232H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
  Adafruit SCD4x: Take a deep breath in...now slowly breathe out. Mmm isn't it wonderful? All that air around us, which we bring into our lungs, extracts oxygen from and then breathes out carbon dioxide. CO2 is essential for life on this planet we call Earth - we and plants take turns using and emitting CO2 in an elegant symbiosis. But it's important to keep that CO2 balanced - you don't want too much around,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
